// Logisim project Project_scoreboard.circ as structural Verilog: 3 circuits, main circuit main
module main (
  input  in_1,
  input  in_2,
  input  in_3,
  input  in_4,
  input  in_5,
  input  in_6,
  input  in_7,
  input  in_8,
  input  in_9,
  input  in_10,
  output Orange,
  output out_12,
  output Purple
);

  wire button_1_out, comparator_1_eq, comparator_2_eq, main_1_p8, main_2_p1, n7447_1_a_2, n7447_1_b_2,
       n7447_1_c_2, n7447_1_d_2, n7447_1_e, n7447_1_f, n7447_1_g, n7447_2_a_2, n7447_2_b_2, n7447_2_c_2,
       n7447_2_d_2, n7447_2_e, n7447_2_f, n7447_2_g;
  wire [3:0] main_1_p4, main_2_p4;

  Button button_1 (.out(button_1_out));
  // _74163built_main main_1: pin names not known; wires that end beside it: button_1_out, 1'b0, 1'b1, main_1_p4[0], main_1_p4[1], main_1_p4[2], main_1_p4[3], main_1_p8
  // _74163built_main main_2: pin names not known; wires that end beside it: main_2_p1, 1'b0, 1'b1, main_2_p4[0], main_2_p4[1], main_2_p4[2], main_2_p4[3], main_1_p8
  Button button_2 (.out(main_2_p1));
  Comparator #(.width(4)) comparator_1 (
    .a(main_1_p4), .b({in_5, in_4, in_3, in_2}), .eq(comparator_1_eq));  // open: gt, lt
  Comparator #(.width(4)) comparator_2 (
    .a(main_2_p4), .b({in_10, in_9, in_8, in_7}), .eq(comparator_2_eq));  // open: gt, lt
  or or_1 (main_1_p8, comparator_1_eq, comparator_2_eq);
  _7447 u_7447_1 (
    .D(main_1_p4[3]), .C(main_1_p4[2]), .B(main_1_p4[1]), .A(main_1_p4[0]), .a_2(n7447_1_a_2),
    .b_2(n7447_1_b_2), .c_2(n7447_1_c_2), .d_2(n7447_1_d_2), .e(n7447_1_e), .f(n7447_1_f), .g(n7447_1_g));
  _7447 u_7447_2 (
    .D(main_2_p4[3]), .C(main_2_p4[2]), .B(main_2_p4[1]), .A(main_2_p4[0]), .a_2(n7447_2_a_2),
    .b_2(n7447_2_b_2), .c_2(n7447_2_c_2), .d_2(n7447_2_d_2), .e(n7447_2_e), .f(n7447_2_f), .g(n7447_2_g));
  _7_Segment_Display u_7_segment_display_1 (
    .g(n7447_1_g), .f(n7447_1_f), .a(n7447_1_a_2), .b(n7447_1_b_2), .e(n7447_1_e), .d(n7447_1_d_2),
    .c(n7447_1_c_2), .dp(in_1));
  _7_Segment_Display u_7_segment_display_2 (
    .g(n7447_2_g), .f(n7447_2_f), .a(n7447_2_a_2), .b(n7447_2_b_2), .e(n7447_2_e), .d(n7447_2_d_2),
    .c(n7447_2_c_2), .dp(in_6));
  Comparator #(.width(4), .mode("unsigned")) comparator_3 (
    .a(main_1_p4), .b(main_2_p4), .gt(Orange), .eq(out_12), .lt(Purple));

  // Notes on the sheet:
  //   Scoreboard
endmodule

module _7447 (
  input  D,
  input  C,
  input  B,
  input  A,
  output a_2,
  output b_2,
  output c_2,
  output d_2,
  output e,
  output f,
  output g
);

  wire and_1_out, and_2_out, and_3_out, and_4_out, and_5_out, and_6_out, and_7_out, and_8_out, and_9_out,
       and_10_out, and_11_out, and_12_out, and_13_out, and_14_out, and_15_out, and_16_out, and_17_out,
       and_18_out, not_1_out, not_2_out, not_3_out, not_4_out, not_5_out, not_6_out, not_7_out, not_8_out,
       not_9_out, not_10_out, not_11_out, not_12_out, not_13_out, not_14_out, not_15_out, not_16_out,
       not_17_out, not_18_out, not_19_out, not_20_out, not_21_out, not_22_out;

  not not_1 (not_1_out, C);
  and and_1 (and_1_out, not_1_out, not_2_out);
  not not_2 (not_2_out, A);
  not not_3 (not_3_out, C);
  and and_2 (and_2_out, not_3_out, B);
  and and_3 (and_3_out, C, A);
  not not_4 (not_4_out, C);
  not not_5 (not_5_out, B);
  and and_4 (and_4_out, not_5_out, not_6_out);
  not not_6 (not_6_out, A);
  and and_5 (and_5_out, B, A);
  not not_7 (not_7_out, B);
  or or_1 (c_2, not_7_out, A, C);
  not not_8 (not_8_out, C);
  and and_6 (and_6_out, not_8_out, not_9_out);
  not not_9 (not_9_out, A);
  not not_10 (not_10_out, C);
  and and_7 (and_7_out, not_10_out, B);
  and and_8 (and_8_out, B, not_11_out);
  not not_11 (not_11_out, A);
  not not_12 (not_12_out, B);
  and and_9 (and_9_out, C, not_12_out, A);
  and and_10 (and_10_out, D, C);
  not not_13 (not_13_out, C);
  and and_11 (and_11_out, not_13_out, not_14_out);
  not not_14 (not_14_out, A);
  and and_12 (and_12_out, B, not_15_out);
  not not_15 (not_15_out, A);
  not not_16 (not_16_out, B);
  and and_13 (and_13_out, not_16_out, not_17_out);
  not not_17 (not_17_out, A);
  and and_14 (and_14_out, C, not_18_out);
  not not_18 (not_18_out, B);
  and and_15 (and_15_out, C, not_19_out);
  not not_19 (not_19_out, A);
  not not_20 (not_20_out, C);
  and and_16 (and_16_out, not_20_out, B);
  and and_17 (and_17_out, C, not_21_out);
  not not_21 (not_21_out, B);
  and and_18 (and_18_out, C, not_22_out);
  not not_22 (not_22_out, A);
  or or_2 (a_2, and_1_out, and_2_out, and_3_out, D);
  or or_3 (b_2, not_4_out, and_4_out, and_5_out);
  or or_4 (d_2, and_6_out, and_7_out, and_8_out, and_9_out, and_10_out);
  or or_5 (e, and_11_out, and_12_out);
  or or_6 (f, and_13_out, and_14_out, and_15_out, D);
  or or_7 (g, and_16_out, and_17_out, and_18_out, D);
endmodule

module _74472 (
  input  D,
  input  C,
  input  B,
  input  A,
  output a_2,
  output b_2,
  output c_2,
  output d_2,
  output e,
  output f,
  output g
);

  wire and_1_out, and_2_out, and_3_out, and_4_out, and_5_out, and_6_out, and_7_out, and_8_out, and_9_out,
       and_10_out, and_11_out, and_12_out, and_13_out, and_14_out, and_15_out, and_16_out, and_17_out,
       and_18_out, and_19_out, and_20_out, and_21_out, and_22_out, and_23_out, and_24_out, and_25_out,
       and_26_out, not_1_out, not_2_out, not_3_out, not_4_out, not_5_out, not_6_out, not_7_out, not_8_out,
       not_9_out, not_10_out, not_11_out, not_12_out, not_13_out, not_14_out, not_15_out, not_16_out,
       not_17_out, not_18_out, not_19_out, not_20_out, not_21_out, not_22_out, not_23_out, not_24_out,
       not_25_out, not_26_out, not_27_out, not_28_out, not_29_out, not_30_out, not_31_out, not_32_out,
       not_33_out, not_34_out, not_35_out, not_36_out, not_37_out, not_38_out, not_39_out, not_40_out,
       not_41_out, not_42_out, not_43_out, not_44_out, not_45_out, not_46_out, not_47_out, not_48_out,
       not_49_out, not_50_out, not_51_out, not_52_out;

  not not_1 (not_1_out, D);
  not not_2 (not_2_out, C);
  and and_1 (and_1_out, not_1_out, not_2_out, not_3_out);
  not not_3 (not_3_out, A);
  not not_4 (not_4_out, D);
  and and_2 (and_2_out, not_4_out, B);
  not not_5 (not_5_out, D);
  and and_3 (and_3_out, not_5_out, C, A);
  and and_4 (and_4_out, D, not_6_out, not_7_out);
  not not_6 (not_6_out, C);
  not not_7 (not_7_out, B);
  not not_8 (not_8_out, D);
  and and_5 (and_5_out, not_8_out, not_9_out);
  not not_9 (not_9_out, C);
  not not_10 (not_10_out, D);
  not not_11 (not_11_out, B);
  and and_6 (and_6_out, not_10_out, not_11_out, not_12_out);
  not not_12 (not_12_out, A);
  not not_13 (not_13_out, C);
  and and_7 (and_7_out, not_13_out, not_14_out);
  not not_14 (not_14_out, B);
  not not_15 (not_15_out, D);
  and and_8 (and_8_out, not_15_out, B, A);
  not not_16 (not_16_out, C);
  and and_9 (and_9_out, not_16_out, not_17_out);
  not not_17 (not_17_out, B);
  not not_18 (not_18_out, D);
  and and_10 (and_10_out, not_18_out, A);
  not not_19 (not_19_out, D);
  and and_11 (and_11_out, not_19_out, C);
  not not_20 (not_20_out, D);
  not not_21 (not_21_out, C);
  not not_22 (not_22_out, A);
  not not_23 (not_23_out, D);
  not not_24 (not_24_out, C);
  not not_25 (not_25_out, D);
  not not_26 (not_26_out, A);
  not not_27 (not_27_out, D);
  not not_28 (not_28_out, B);
  not not_29 (not_29_out, C);
  not not_30 (not_30_out, B);
  not not_31 (not_31_out, C);
  and and_12 (and_12_out, not_31_out, not_32_out, not_33_out);
  not not_32 (not_32_out, B);
  not not_33 (not_33_out, A);
  not not_34 (not_34_out, D);
  and and_13 (and_13_out, not_34_out, B, not_35_out);
  not not_35 (not_35_out, A);
  not not_36 (not_36_out, D);
  and and_14 (and_14_out, not_36_out, not_37_out, not_38_out);
  not not_37 (not_37_out, B);
  not not_38 (not_38_out, A);
  not not_39 (not_39_out, D);
  and and_15 (and_15_out, not_39_out, C, not_40_out);
  not not_40 (not_40_out, B);
  not not_41 (not_41_out, D);
  and and_16 (and_16_out, not_41_out, C, not_42_out);
  not not_42 (not_42_out, A);
  and and_17 (and_17_out, D, not_43_out, not_44_out);
  not not_43 (not_43_out, C);
  not not_44 (not_44_out, B);
  not not_45 (not_45_out, D);
  and and_18 (and_18_out, not_45_out, not_46_out, B);
  not not_46 (not_46_out, C);
  not not_47 (not_47_out, D);
  and and_19 (and_19_out, not_47_out, C, not_48_out);
  not not_48 (not_48_out, B);
  not not_49 (not_49_out, D);
  and and_20 (and_20_out, not_49_out, C, not_50_out);
  not not_50 (not_50_out, A);
  and and_21 (and_21_out, D, not_51_out, not_52_out);
  not not_51 (not_51_out, C);
  not not_52 (not_52_out, B);
  or or_1 (a_2, and_1_out, and_2_out, and_3_out, and_4_out);
  or or_2 (b_2, and_5_out, and_6_out, and_7_out, and_8_out);
  or or_3 (c_2, and_9_out, and_10_out, and_11_out);
  and and_22 (and_22_out, not_20_out, not_21_out, not_22_out);
  and and_23 (and_23_out, not_23_out, not_24_out, B);
  and and_24 (and_24_out, not_25_out, B, not_26_out);
  and and_25 (and_25_out, not_27_out, C, not_28_out, A);
  and and_26 (and_26_out, D, not_29_out, not_30_out);
  or or_4 (e, and_12_out, and_13_out);
  or or_5 (f, and_14_out, and_15_out, and_16_out, and_17_out);
  or or_6 (g, and_18_out, and_19_out, and_20_out, and_21_out);
  or or_7 (d_2, and_22_out, and_23_out, and_24_out, and_25_out, and_26_out);
endmodule
